# Fritzing sketch EsquemaConexiónProyecto (saved by Fritzing 0.9.3b)

parts:
  Mod1 = Raspberry Pi 4B
  KY-1 = Keyes Relay [package=THT]
  KY-2 = Keyes Relay [package=THT]
  KY-3 = Keyes Relay [package=THT]
  KY-4 = Keyes Relay [package=THT]
  KY-5 = Keyes Relay [package=THT]
  J1 = Basic Servo  # not connected
  IC1 = Rasberry Pi NIOR Camera [chip_label=IC package="DIP (Dual Inline) [THT]"]  # not connected
  Power_plug1 = Power plug
  LED1 = LEDs [package=led10mm]
  LED2 = LEDs [package=led10mm]
  Power_plug2 = Power plug
  LED3 = LEDs [package=led10mm]
  LED4 = LEDs [package=led10mm]
  LED5 = LEDs [package=led10mm]

nets:
  N1: Mod1.GPIO13, KY-5.ground
  N2: Mod1.GPIO19, KY-4.ground
  N3: Mod1.GPIO16, KY-2.ground
  N4: Mod1.GPIO20, KY-1.ground
  N5: Mod1.GPIO21, KY-3.ground
  N6: KY-1.signal, Power_plug1.VCC
  N7: KY-1.C, Power_plug2.VCC
  N8: KY-1.NO, LED1.C
  N9: KY-2.NO, LED2.C
  N10: KY-3.NO, LED3.C
  N11: KY-4.NO, LED4.C
  N12: KY-5.power, Power_plug1.GND
  N13: KY-5.NO, LED5.C
  N14: LED1.A, Power_plug2.GND

notes:
  Fuente 5 V DC
  FUENTE 110V AC
  Diseño e implementación de un sistema de seguridad domótico con Raspberry Pi y una aplicación Móvil.
  Proyecto / Grupo 4
  Banchón Valdiviezo Melissa Lissette
  Lazo Ramírez Brandon Andrés

custom parts:
  Keyes Relay: The Keyes 5V relay module is suitable for SCM development, home appliance control. It uses a 5V~12V TIL control signal which can control DC / AC signal.
  Rasberry Pi NIOR Camera: Camera
  LEDs: LEDs Standard schematic elements and footprints for 5mm, 3mm, 1206, and 0603 sized LEDs. 5mm - Spark Fun Electronics SKU : COM-00529 (and others)
